# Fritzing sketch Wiring Diagram (saved by Fritzing 0.9.3b)
breadboards: 2

parts:
  U1 = ESP32-38PinWide [part_number=ESP32-38PinWide]
  L298N1 = L298N DC motor driver
  L298N2 = L298N DC motor driver  # not connected
  M1 = DC Motor  # not connected
  M2 = DC Motor  # not connected
  M3 = DC Motor  # not connected
  M4 = DC Motor  # not connected
  M5 = RioRand LM2596
  HC-SR04_Sensor_1 = HC-SR04 Ultrasonic Distance Sensor
  M6 = fc-51 [package=THT]
  M7 = fc-51 [package=THT]
  VCC3 = Battery
  VCC4 = Battery
  VCC5 = Battery  # not connected
  U2 = SWITCH-SPST-2 [package=r_sw_th]
  M8 = Dagu DGServo 9g (Pan and tilt) [part_number=RS001B]
  LCD1 = LCD screen  # not connected

nets:
  N1: U1.GPIO34, M6.pin1
  N2: U1.GPIO35, M7.pin1
  N3: U1.GPIO32, HC-SR04_Sensor_1.ECHO
  N4: U1.GPIO33, HC-SR04_Sensor_1.TRIG
  N5: U1.GPIO25, L298N1.ENB
  N6: U1.GPIO26, L298N1.IN4
  N7: U1.GPIO27, L298N1.IN3
  N8: U1.GPIO14, L298N1.IN2
  N9: U1.GPIO12, L298N1.IN1
  N10: U1.GPIO13, L298N1.ENA
  VCC: U1.VIN, M5.Pin_3, HC-SR04_Sensor_1.VCC, M6.pin3, M7.pin3, M8.vcc
  N11: M5.Pin_1, M5.Pin_4, M6.pin2, U2.P, M8.gnd
  N12: M5.Pin_2, HC-SR04_Sensor_1.GND, M7.pin2, VCC3.-
  N13: VCC4.+, U2.O

custom parts:
  ESP32-38PinWide: Generic 38-Pin ESP32 with wide format (only access to one side of pins on a breadboard) based on Stephen Lilley's HiLetgo ESP-WROOM-32 ESP32 ESP-32S Development Board.
  L298N DC motor driver: 2x DC motor driver with 78M05 positive voltage regulator (7..35 V) L298N: max 46 V, 2 A Set 5 V Enable jumper to enable 5 V regultor (needed for the L298N) and +5 V output at screw terminal or supply external +5 V at screw terminal Set ENA and/or ENB to +5 V to enable motor permanently or supply ENA and/or ENB with PWM signal IN1 and IN2 set rotation directory for motor A (OUT1/OUT2) IN2 and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
